# Fritzing sketch 5V昇圧DCDCシールド (saved by Fritzing 0.9.2b)
perfboards: 1

parts:
  IOL = female pin header, 8 pins [form="♀ (female)"]  # not connected
  IOH = female pin header, 10 pins [form="♀ (female)"]
  AD = female pin header, 6 pins [form="♀ (female)"]  # not connected
  POWER = female pin header, 8 pins [form="♀ (female)"]
  DCDC5V = XCL101 [package=sc70-6]

nets:
  GND: IOH.pin4, POWER.pin6, POWER.pin7, DCDC5V.VSS
  N1: POWER.pin5, DCDC5V.Vout
  N2: POWER.pin8, DCDC5V.Vbat, DCDC5V.CE

custom parts:
  XCL101: AE-XCL101C331BR
