# Fritzing sketch ArduinoProMini基板変換 (saved by Fritzing 0.9.2b)
perfboards: 1

parts:
  IOH = female pin header, 10 pins [form="♀ (female)"]
  IOL = female pin header, 8 pins [form="♀ (female)"]
  AD = female pin header, 6 pins [form="♀ (female)"]
  Power = female pin header, 8 pins [form="♀ (female)"]
  Reset = Momentary Switch [package=ksa_sealed_tac_switch]
  Power_plug = AE-DC-POWER-JACK-DIP [part_number=AE-DC-POWER-JACK-DIP]
  Pro_Mini_3V3_8MHz = Arduino Pro Mini v13

nets:
  N1: IOH.pin4, Power.pin7, Pro_Mini_3V3_8MHz.GND
  N2: IOH.pin5, Pro_Mini_3V3_8MHz.D13/SCK
  N3: IOH.pin6, Pro_Mini_3V3_8MHz.D12/MISO
  N4: IOH.pin7, Pro_Mini_3V3_8MHz.D11_PWM/MOSI
  N5: IOH.pin8, Pro_Mini_3V3_8MHz.D10_PWM/SS
  N6: IOH.pin9, Pro_Mini_3V3_8MHz.D9_PWM
  N7: IOH.pin10, Pro_Mini_3V3_8MHz.D8
  N8: IOL.pin1, Pro_Mini_3V3_8MHz.D7
  N9: IOL.pin2, Pro_Mini_3V3_8MHz.D6_PWM
  N10: IOL.pin3, Pro_Mini_3V3_8MHz.D5_PWM
  N11: IOL.pin4, Pro_Mini_3V3_8MHz.D4
  N12: IOL.pin5, Pro_Mini_3V3_8MHz.D3_PWM
  N13: IOL.pin6, Pro_Mini_3V3_8MHz.D2
  N14: IOL.pin7, Pro_Mini_3V3_8MHz.D1/RX
  N15: IOL.pin8, Pro_Mini_3V3_8MHz.D0/TX
  N16: AD.pin1, Pro_Mini_3V3_8MHz.A0
  N17: AD.pin2, Pro_Mini_3V3_8MHz.A1
  N18: AD.pin3, Pro_Mini_3V3_8MHz.A2
  N19: AD.pin4, Pro_Mini_3V3_8MHz.A3
  N20: AD.pin5, Pro_Mini_3V3_8MHz.A4
  N21: AD.pin6, Pro_Mini_3V3_8MHz.A5
  N22: Power.pin3, Reset.2, Pro_Mini_3V3_8MHz.RESET
  N23: Power.pin4, Pro_Mini_3V3_8MHz.VCC
  N24: Power.pin6, Reset.4, Power_plug.GND#0, Power_plug.GND#2
  N25: Power.pin8, Power_plug.VCC#5, Pro_Mini_3V3_8MHz.RAW

custom parts:
  AE-DC-POWER-JACK-DIP: 秋月電子通商 K-05148
  Arduino Pro Mini v13: It's blue! It's thin! It's the Arduino Pro Mini! SparkFun's minimal design approach to Arduino. This is a 5V Arduino running the 16MHz bootloader. Arduino Pro Mini does not come with connectors populated so that you can solder in any connector or wire with any orientation you need. We recommend first time Arduino users start with the Uno R3. It's a great board that will get you up and running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
