# Fritzing sketch RTC8564NBシールド (saved by Fritzing 0.9.2b)
perfboards: 1

parts:
  IOH = female pin header, 10 pins [form="♀ (female)"]
  IOL = female pin header, 8 pins [form="♀ (female)"]
  AD = female pin header, 6 pins [form="♀ (female)"]
  BAT = Battery Holders [package=battcom_20mm_pth]
  J1 = male pin header, 15 pins [form="♂ (male)"]
  D1 = Schottky Diode [part_number=1N5817 package="300 mil [THT]"]
  D2 = Schottky Diode [part_number=1N5817 package="300 mil [THT]"]
  INT = male pin header, 15 pins [form="♂ (male)"]
  Power = female pin header, 8 pins [form="♀ (female)"]
  S1 = Akizuki slide switch IS-1250
  J2 = Arduino R3 6pin male header [package=THT]  # not connected
  RTC1 = RTC-8564NB [package="Module(DIP 8P)"]

nets:
  GND: IOH.pin4, BAT.-, Power.pin6, Power.pin7, RTC1.GND
  N1: IOH.pin5, J1.pin1
  N2: IOH.pin6, J1.pin2
  N3: IOH.pin7, J1.pin3
  N4: IOH.pin8, J1.pin4
  N5: IOH.pin9, J1.pin5
  N6: IOH.pin10, J1.pin6
  N7: IOL.pin1, J1.pin8
  N8: IOL.pin2, J1.pin9
  N9: IOL.pin3, J1.pin10
  N10: IOL.pin4, J1.pin11
  N11: IOL.pin5, J1.pin12
  N12: IOL.pin6, J1.pin13
  N13: IOL.pin7, J1.pin14
  N14: IOL.pin8, J1.pin15
  N15: AD.pin5, RTC1.SDA
  N16: AD.pin6, RTC1.SCL
  N17: BAT.+, D2.anode
  N18: D1.cathode, D2.cathode, RTC1.VDD
  N19: D1.anode, S1.pin1, S1.pin4
  N20: INT.pin1, INT.pin2, INT.pin3, INT.pin4, INT.pin5, INT.pin6, INT.pin7, INT.pin8, INT.pin9, INT.pin10, INT.pin11, INT.pin12, INT.pin13, INT.pin14, INT.pin15, RTC1.INT
  N21: Power.pin4, S1.pin2, S1.pin5
  N22: Power.pin5, S1.pin0, S1.pin3

custom parts:
  Akizuki slide switch IS-1250: Akizuki slide switch is-1250 (P-01665)
  Arduino R3 6pin male header: Pin header for arduino R3
  RTC-8564NB: Real Time Clock Module and I2C-BUS interface method. This product is a module of the SON 8-pin DIP package. Supply voltage 1.8-5.5V original version by KimuShige
