# Fritzing sketch Xbeeシールド (saved by Fritzing 0.9.2b)
perfboards: 1

parts:
  Xbee = XBEE-1 [package=xbee-1]
  IOH = female pin header, 10 pins [form="♀ (female)"]
  J1 = male pin header, 15 pins [form="♂ (male)"]
  IOL = female pin header, 8 pins [form="♀ (female)"]
  Power = female pin header, 8 pins [form="♀ (female)"]
  AD = female pin header, 6 pins [form="♀ (female)"]  # not connected
  INT = male pin header, 15 pins [form="♂ (male)"]
  J2 = male pin header, 15 pins [form="♂ (male)"]
  Tx = male pin header, 15 pins [form="♂ (male)"]
  J3 = male pin header, 15 pins [form="♂ (male)"]
  Rx = male pin header, 15 pins [form="♂ (male)"]

nets:
  N1: Xbee.VDD, Power.pin4
  N2: Xbee.DOUT, Tx.pin1, Tx.pin2, Tx.pin3, Tx.pin4, Tx.pin5, Tx.pin6, Tx.pin7, Tx.pin8, Tx.pin9, Tx.pin10, Tx.pin11, Tx.pin12, Tx.pin13, Tx.pin14, Tx.pin15
  N3: Xbee.DIN, Rx.pin1, Rx.pin2, Rx.pin3, Rx.pin4, Rx.pin5, Rx.pin6, Rx.pin7, Rx.pin8, Rx.pin9, Rx.pin10, Rx.pin11, Rx.pin12, Rx.pin13, Rx.pin14, Rx.pin15
  N4: Xbee.DIO12, INT.pin1, INT.pin2, INT.pin3, INT.pin4, INT.pin5, INT.pin6, INT.pin7, INT.pin8, INT.pin9, INT.pin10, INT.pin11, INT.pin12, INT.pin13, INT.pin14, INT.pin15
  N5: Xbee.DIO11, Power.pin3
  N6: Xbee.GND, Power.pin6
  N7: IOH.pin5, J1.pin1, J2.pin1, J3.pin1
  N8: IOH.pin6, J1.pin2, J2.pin2, J3.pin2
  N9: IOH.pin7, J1.pin3, J2.pin3, J3.pin3
  N10: IOH.pin8, J1.pin4, J2.pin4, J3.pin4
  N11: IOH.pin9, J1.pin5, J2.pin5, J3.pin5
  N12: IOH.pin10, J1.pin6, J2.pin6, J3.pin6
  N13: J1.pin8, IOL.pin1, J2.pin8, J3.pin8
  N14: J1.pin9, IOL.pin2, J2.pin9, J3.pin9
  N15: J1.pin10, IOL.pin3, J2.pin10, J3.pin10
  N16: J1.pin11, IOL.pin4, J2.pin11, J3.pin11
  N17: J1.pin12, IOL.pin5, J2.pin12, J3.pin12
  N18: J1.pin13, IOL.pin6, J2.pin13, J3.pin13
  N19: J1.pin14, IOL.pin7, J2.pin14, J3.pin14
  N20: J1.pin15, IOL.pin8, J2.pin15, J3.pin15
